# Fritzing sketch schematic project (saved by Fritzing 0.9.3b)

parts:
  U3 = ESP32-38PinWide [part_number=ESP32-38PinWide]
  Part3 = LCD1602-I2C
  S2 = LDR light sensor [package=THT]
  WATER_PUMP2 = water pump/motor
  U4 = Mini-360 DC-DC Buck converter [package=THT]
  DHT2 = Humidity and Temperature Sensor DHT11
  VCC2 = Battery block 9V
  IC2 = DIP - 6 pins [chip_label="5V RELAY" package="DIP (Dual Inline) [THT]"]
  Capacitive_Soil_Moisture_Sensor2 = DFRobot Capacitive Soil Moisture Sensor V1.0 [part_number=SEN0193]

nets (from the breadboard view):
  VCC: U3.3.3, S2.pin3, DHT2.Vcc, Capacitive_Soil_Moisture_Sensor2.VCC
  N1: U3.GPIO36, Capacitive_Soil_Moisture_Sensor2.A
  N2: U3.GPIO39, S2.pin1
  GND: U3.GND, Part3.GND, S2.pin2, U4.OUT-, DHT2.GND_1, DHT2.GND_2, IC2.CO, Capacitive_Soil_Moisture_Sensor2.GND
  VIN: U3.VIN, Part3.VCC, U4.OUT+, IC2.DC+
  N3: U3.GPIO17, DHT2.Data-signal
  N4: U3.GPIO5, IC2.IN
  N5: U3.GPIO21, Part3.SDA
  N6: U3.GPIO22, Part3.SCL
  N7: WATER_PUMP2.pin_1, U4.IN+, VCC2.+
  N8: WATER_PUMP2.pin_2, IC2.NC
  N9: U4.IN-, VCC2.-

custom parts:
  ESP32-38PinWide: Generic 38-Pin ESP32 with wide format (only access to one side of pins on a breadboard) based on Stephen Lilley's HiLetgo ESP-WROOM-32 ESP32 ESP-32S Development Board.
  LCD1602-I2C: A standard character display, usually with 2x16 characters. Comes in many colors with LCM1602 IIC attached.
  LDR light sensor: Light sensor module. 3.3 V to 5V power.
  water pump/motor: WATER PUMP BY ARDUBLOCKTR
  Mini-360 DC-DC Buck converter: Mini-360 DC-DC Buck converter. Tiny buck step down voltage converter, input voltage 4.75 to 23V output 1 to 17V adjustable. Available from ebay and the like.
  Humidity and Temperature Sensor DHT11: Digital relative humidity & temperature sensor DHT11
  DIP - 6 pins: A DIP stand-in part for whatever IC you want. With 6 pins on a 300mil dual inline package (DIP) footprint.
  DFRobot Capacitive Soil Moisture Sensor V1.0: DFRobot Capacitive Soil Moisture Sensor V1.0 This product measures soil moisture levels by capacitive sensing, rather than resistive sensing like other types of moisture sensor. It is made of a corrosion resistant material giving it a long service life. Insert it into soil and impress your friends with the real-time soil moisture data! The product includes an on-board voltage regulator which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
